// Logisim project question1.circ as structural Verilog: 1 circuit, main circuit main
module main (
  input  b1,
  input  b2,
  input  b3,
  output s0,
  output s1
);

  wire and_1_out, and_2_out, and_3_out, and_4_out, and_5_out, and_6_out, and_7_out, not_1_out, not_2_out,
       not_3_out, not_4_out, not_5_out, not_6_out;

  not not_1 (not_1_out, b1);
  not not_2 (not_2_out, b2);
  not not_3 (not_3_out, b1);
  not not_4 (not_4_out, b3);
  not not_5 (not_5_out, b2);
  not not_6 (not_6_out, b3);
  and and_1 (and_1_out, b2, b3);
  and and_2 (and_2_out, b1, b3);
  and and_3 (and_3_out, b1, b2);
  and and_4 (and_4_out, not_1_out, not_2_out, b3);
  and and_5 (and_5_out, not_3_out, b2, not_4_out);
  and and_6 (and_6_out, b1, not_5_out, not_6_out);
  and and_7 (and_7_out, b1, b2, b3);
  or or_1 (s1, and_1_out, and_2_out, and_3_out);
  or or_2 (s0, and_4_out, and_5_out, and_6_out, and_7_out);
endmodule
